# Fritzing sketch circuito (saved by Fritzing 0.9.3b)

parts:
  ESP32_-_Back1 = ESP32 - CAM
  M1 = DC Motor
  M2 = DC Motor
  S1 = H-Bridge with L298N
  VCC1 = Battery
  J1 = Basic Servo
  J2 = Basic Servo

nets:
  N1: ESP32_-_Back1.GPIO2, S1.IN2
  N2: ESP32_-_Back1.GPIO14, J1.pulse
  N3: ESP32_-_Back1.GPIO15, J2.pulse
  N4: ESP32_-_Back1.GPIO13, S1.ENA
  N5: ESP32_-_Back1.GPIO12, S1.ENB
  GND: ESP32_-_Back1.GND, S1.GND, VCC1.-
  N6: ESP32_-_Back1.GPIO3_/_RX, S1.IN3
  N7: M1.pin_1, S1.M2-02
  N8: M1.pin_2, S1.M2-01
  N9: M2.pin_1, S1.M1-02
  N10: M2.pin_2, S1.M1-01
  N11: S1.12V, VCC1.+
  5V: S1.5V, J2.vcc
  GND_2: J1.gnd, J2.gnd

custom parts:
  ESP32 - CAM: The ESP32-CAM has a very competitive small-size camera module that can operate independently as a minimum system with a footprint of only 27*40.5*4.5mm and a deep sleep current of up to 6mA.
  H-Bridge with L298N: h-bridge
